// Logisim project mips-cpu.circ as structural Verilog: 7 circuits, main circuit main
module main (
);

  wire alu_1_zero, ALUSrc, and_1_out, Branch, Clock, Jump, MemRead, MemToReg, MemWrite, RegDst, RegWrite;
  wire [1:0] ALU_Op;
  wire [3:0] alu_control_1_alu_control;
  wire [4:0] multiplexer_1_out;
  wire [5:0] opcode;
  wire [25:0] instruction_memory_1_instruction;
  wire [31:0] adder_1_out, adder_2_out, alu_1_result, bit_extender_1_out, data_memory_1_read_data,
       multiplexer_2_out, multiplexer_3_out, multiplexer_4_out, multiplexer_5_out, PC_q,
       register_file_1_read_data_1, register_file_1_read_data_2, shifter_1_out;

  Clock clock_1 (.out(Clock));
  Register #(.width(32)) PC (.D(multiplexer_4_out), .Q(PC_q), .clk(Clock));  // open: en, clr
  Adder #(.width(32)) adder_1 (.a(32'h1), .b(PC_q), .out(adder_1_out));  // open: cin, cout
  Control control_1 (
    .opcode(opcode), .Jump(Jump), .Branch(Branch), .MemToReg(MemToReg), .MemRead(MemRead),
    .MemWrite(MemWrite), .RegWrite(RegWrite), .RegDst(RegDst), .ALUSrc(ALUSrc), .ALUOp(ALU_Op));
  Instruction_Memory instruction_memory_1 (.Address(PC_q), .Instruction({opcode, instruction_memory_1_instruction}));
  Multiplexer #(.width(5), .enable("false")) multiplexer_1 (
    .in0(instruction_memory_1_instruction[20:16]), .in1(instruction_memory_1_instruction[15:11]),
    .out(multiplexer_1_out), .sel(RegDst));
  Register_File register_file_1 (
    .Read_Reg_1(instruction_memory_1_instruction[25:21]), .Clock(Clock), .Write_Reg(multiplexer_1_out),
    .RegWrite(RegWrite), .Write_Data(multiplexer_5_out),
    .Read_Reg_2(instruction_memory_1_instruction[20:16]), .Read_Data_1(register_file_1_read_data_1),
    .Read_Data_2(register_file_1_read_data_2));
  assign bit_extender_1_out = {{16{instruction_memory_1_instruction[15]}}, instruction_memory_1_instruction[15:0]};  // Bit_Extender bit_extender_1
  Shifter #(.width(32)) shifter_1 (.in(bit_extender_1_out), .\dist (5'b00010), .out(shifter_1_out));
  Multiplexer #(.width(32), .enable("false")) multiplexer_2 (
    .in0(register_file_1_read_data_2), .in1(bit_extender_1_out), .out(multiplexer_2_out), .sel(ALUSrc));
  ALU_Control alu_control_1 (
    .ALU_Op(ALU_Op), .funct(instruction_memory_1_instruction[5:0]), .ALU_Control(alu_control_1_alu_control));
  Adder #(.width(32)) adder_2 (.a(adder_1_out), .b(shifter_1_out), .out(adder_2_out));  // open: cin, cout
  ALU alu_1 (
    .A(register_file_1_read_data_1), .B(multiplexer_2_out), .Result(alu_1_result), .Zero(alu_1_zero),
    .ALU_Control(alu_control_1_alu_control));
  and and_1 (and_1_out, Branch, alu_1_zero);
  Multiplexer #(.width(32), .enable("false")) multiplexer_3 (
    .in0(adder_1_out), .in1(adder_2_out), .out(multiplexer_3_out), .sel(and_1_out));
  Multiplexer #(.width(32), .enable("false")) multiplexer_4 (
    .in0(multiplexer_3_out), .in1({adder_1_out[31:28], instruction_memory_1_instruction, 2'b00}),
    .out(multiplexer_4_out), .sel(Jump));
  Multiplexer #(.width(32), .enable("false")) multiplexer_5 (
    .in0(alu_1_result), .in1(data_memory_1_read_data), .out(multiplexer_5_out), .sel(MemToReg));
  Data_Memory data_memory_1 (
    .Address(alu_1_result), .Write_Data(register_file_1_read_data_2), .MemRead(MemRead), .MemWrite(MemWrite),
    .Read_Data(data_memory_1_read_data));

  // Notes on the sheet:
  //   PC + 4
  //   Señales de Control
  //   rs
  //   rt
  //   rd
  //   Jump Address
  //   ####   ALU Control   ####
  //   0000    AND
  //   0001    OR
  //   0010    ADD
  //   0110    SUB
  //   1100    NOR
  //   funct
  //   imm
  //   ALU Control
  //   Branch Address
  //   MIPS CPU - Single Clock Cycle
endmodule

module ALU (
  input  [31:0] A,
  input  [31:0] B,
  input  [3:0] ALU_Control,
  output [31:0] Result,
  output Zero
);

  wire [31:0] adder_1_out, and_1_out, multiplexer_1_out, multiplexer_2_out, not_1_out, not_2_out, or_1_out;

  assign not_1_out = ~A;  // NOT_Gate not_1, 32 bits wide
  assign not_2_out = ~B;  // NOT_Gate not_2, 32 bits wide
  Multiplexer #(.width(32), .enable("false")) multiplexer_1 (
    .in0(A), .in1(not_1_out), .out(multiplexer_1_out), .sel(ALU_Control[3]));
  Multiplexer #(.width(32), .enable("false")) multiplexer_2 (
    .in0(B), .in1(not_2_out), .out(multiplexer_2_out), .sel(ALU_Control[2]));
  assign and_1_out = multiplexer_1_out & multiplexer_2_out;  // AND_Gate and_1, 32 bits wide
  assign or_1_out = multiplexer_1_out | multiplexer_2_out;  // OR_Gate or_1, 32 bits wide
  Adder #(.width(32)) adder_1 (
    .a(multiplexer_1_out), .b(multiplexer_2_out), .out(adder_1_out), .cin(ALU_Control[2]));  // open: cout
  Multiplexer #(.select(2), .width(32), .enable("false")) multiplexer_3 (
    .in0(and_1_out), .in1(or_1_out), .in2(adder_1_out), .out(Result), .sel(ALU_Control[1:0]));  // open: in3
  nor nor_1 (Zero, Result[0], Result[1], Result[2], Result[3], Result[4], Result[5], Result[6], Result[7], Result[8], Result[9], Result[10], Result[11], Result[12], Result[13], Result[14], Result[15], Result[16], Result[17], Result[18], Result[19], Result[20], Result[21], Result[22], Result[23], Result[24], Result[25], Result[26], Result[27], Result[28], Result[29], Result[30], Result[31]);

  // Other names for the same wires on the sheet: Operation[1:0] = ALU_Control[1:0]; B_Invert = ALU_Control[2];
  //   Carry_In = ALU_Control[2]; A_Invert = ALU_Control[3]

  // Notes on the sheet:
  //   ####   ALU Control   ####
  //   0000    AND
  //   0001    OR
  //   0010    ADD
  //   0110    SUB
  //   1100    NOR
endmodule

module Control (
  input  [5:0] opcode,
  output Jump,
  output Branch,
  output MemToReg,
  output MemRead,
  output MemWrite,
  output RegWrite,
  output RegDst,
  output ALUSrc,
  output [1:0] ALUOp
);

  and Tipo_R (ALUOp[1], ~opcode[5], ~opcode[4], ~opcode[3], ~opcode[2], ~opcode[1], ~opcode[0]);  // AND_Gate
  and lw (MemRead, opcode[5], ~opcode[4], ~opcode[3], ~opcode[2], opcode[1], opcode[0]);  // AND_Gate
  and sw (MemWrite, opcode[5], ~opcode[4], opcode[3], ~opcode[2], opcode[1], opcode[0]);  // AND_Gate
  and beq (ALUOp[0], ~opcode[5], ~opcode[4], ~opcode[3], opcode[2], ~opcode[1], ~opcode[0]);  // AND_Gate
  and j (Jump, ~opcode[5], ~opcode[4], ~opcode[3], ~opcode[2], opcode[1], ~opcode[0]);  // AND_Gate
  or or_1 (RegWrite, ALUOp[1], MemRead);
  or or_2 (ALUSrc, MemWrite, MemRead);

  assign Branch = ALUOp[0];
  assign MemToReg = MemRead;
  assign RegDst = ALUOp[1];

  // Notes on the sheet:
  //   0x00
  //   0x23
  //   0x2b
  //   0x04
  //   0x02
  //   ALUOp 1
  //   ALUOp 0
endmodule

module ALU_Control (
  input  [1:0] ALU_Op,
  input  [5:0] funct,
  output [3:0] ALU_Control
);

  wire and_1_out;

  or or_1 (ALU_Control[1], ~ALU_Op[1], ~funct[2]);  // OR_Gate
  or or_2 (ALU_Control[2], ALU_Op[0], and_1_out);
  and and_1 (and_1_out, ALU_Op[1], funct[1]);
  and and_2 (ALU_Control[0], ALU_Op[1], funct[0], funct[2]);

  assign ALU_Control[3] = 1'b0;
endmodule

module Data_Memory (
  input  [31:0] Address,
  input  [31:0] Write_Data,
  input  MemRead,
  input  MemWrite,
  output [31:0] Read_Data
);

  RAM #(.addrWidth(24), .dataWidth(32), .bus("separate")) ram_1 (
    .addr(Address[23:0]), .din(Write_Data), .data(Read_Data), .str(MemWrite), .clk(MemWrite), .ld(MemRead));  // open: sel, clr
endmodule

module Register_File (
  input  [4:0] Read_Reg_1,
  input  Clock,
  input  [4:0] Write_Reg,
  input  RegWrite,
  input  [31:0] Write_Data,
  input  [4:0] Read_Reg_2,
  output [31:0] Read_Data_1,
  output [31:0] Read_Data_2
);

  wire [31:0] demultiplexer_1_out0, demultiplexer_1_out1, demultiplexer_1_out2, demultiplexer_1_out3,
       demultiplexer_1_out4, demultiplexer_1_out5, demultiplexer_1_out6, demultiplexer_1_out7,
       demultiplexer_1_out8, demultiplexer_1_out9, demultiplexer_1_out10, demultiplexer_1_out11,
       demultiplexer_1_out12, demultiplexer_1_out13, demultiplexer_1_out14, demultiplexer_1_out15,
       demultiplexer_1_out16, demultiplexer_1_out17, demultiplexer_1_out18, demultiplexer_1_out19,
       demultiplexer_1_out20, demultiplexer_1_out21, demultiplexer_1_out22, demultiplexer_1_out23,
       demultiplexer_1_out24, demultiplexer_1_out25, demultiplexer_1_out26, demultiplexer_1_out27,
       demultiplexer_1_out28, demultiplexer_1_out29, demultiplexer_1_out30, demultiplexer_1_out31,
       register_1_q, register_2_q, register_3_q, register_4_q, register_5_q, register_6_q, register_7_q,
       register_8_q, register_9_q, register_10_q, register_11_q, register_12_q, register_13_q, register_14_q,
       register_15_q, register_16_q, register_17_q, register_18_q, register_19_q, register_20_q,
       register_21_q, register_22_q, register_23_q, register_24_q, register_25_q, register_26_q,
       register_27_q, register_28_q, register_29_q, register_30_q, register_31_q, register_32_q;

  Demultiplexer #(.select(5), .width(32), .tristate("true")) demultiplexer_1 (
    .out0(demultiplexer_1_out0), .out1(demultiplexer_1_out1), .out2(demultiplexer_1_out2),
    .out3(demultiplexer_1_out3), .out4(demultiplexer_1_out4), .out5(demultiplexer_1_out5),
    .out6(demultiplexer_1_out6), .out7(demultiplexer_1_out7), .out8(demultiplexer_1_out8),
    .out9(demultiplexer_1_out9), .out10(demultiplexer_1_out10), .out11(demultiplexer_1_out11),
    .out12(demultiplexer_1_out12), .out13(demultiplexer_1_out13), .out14(demultiplexer_1_out14),
    .out15(demultiplexer_1_out15), .out16(demultiplexer_1_out16), .out17(demultiplexer_1_out17),
    .out18(demultiplexer_1_out18), .out19(demultiplexer_1_out19), .out20(demultiplexer_1_out20),
    .out21(demultiplexer_1_out21), .out22(demultiplexer_1_out22), .out23(demultiplexer_1_out23),
    .out24(demultiplexer_1_out24), .out25(demultiplexer_1_out25), .out26(demultiplexer_1_out26),
    .out27(demultiplexer_1_out27), .out28(demultiplexer_1_out28), .out29(demultiplexer_1_out29),
    .out30(demultiplexer_1_out30), .out31(demultiplexer_1_out31), .in(Write_Data), .sel(Write_Reg),
    .en(RegWrite));
  Register #(.width(32)) register_1 (.D(demultiplexer_1_out0), .Q(register_1_q), .clk(Clock));  // open: en, clr
  Register #(.width(32)) register_2 (.D(demultiplexer_1_out4), .Q(register_2_q), .clk(Clock));  // open: en, clr
  Register #(.width(32)) register_3 (.D(demultiplexer_1_out8), .Q(register_3_q), .clk(Clock));  // open: en, clr
  Register #(.width(32)) register_4 (.D(demultiplexer_1_out12), .Q(register_4_q), .clk(Clock));  // open: en, clr
  Register #(.width(32)) register_5 (.D(demultiplexer_1_out16), .Q(register_5_q), .clk(Clock));  // open: en, clr
  Register #(.width(32)) register_6 (.D(demultiplexer_1_out20), .Q(register_6_q), .clk(Clock));  // open: en, clr
  Register #(.width(32)) register_7 (.D(demultiplexer_1_out24), .Q(register_7_q), .clk(Clock));  // open: en, clr
  Register #(.width(32)) register_8 (.D(demultiplexer_1_out28), .Q(register_8_q), .clk(Clock));  // open: en, clr
  Register #(.width(32)) register_9 (.D(demultiplexer_1_out1), .Q(register_9_q), .clk(Clock));  // open: en, clr
  Register #(.width(32)) register_10 (.D(demultiplexer_1_out5), .Q(register_10_q), .clk(Clock));  // open: en, clr
  Register #(.width(32)) register_11 (.D(demultiplexer_1_out9), .Q(register_11_q), .clk(Clock));  // open: en, clr
  Register #(.width(32)) register_12 (.D(demultiplexer_1_out13), .Q(register_12_q), .clk(Clock));  // open: en, clr
  Register #(.width(32)) register_13 (.D(demultiplexer_1_out17), .Q(register_13_q), .clk(Clock));  // open: en, clr
  Register #(.width(32)) register_14 (.D(demultiplexer_1_out21), .Q(register_14_q), .clk(Clock));  // open: en, clr
  Register #(.width(32)) register_15 (.D(demultiplexer_1_out25), .Q(register_15_q), .clk(Clock));  // open: en, clr
  Register #(.width(32)) register_16 (.D(demultiplexer_1_out29), .Q(register_16_q), .clk(Clock));  // open: en, clr
  Register #(.width(32)) register_17 (.D(demultiplexer_1_out2), .Q(register_17_q), .clk(Clock));  // open: en, clr
  Register #(.width(32)) register_18 (.D(demultiplexer_1_out6), .Q(register_18_q), .clk(Clock));  // open: en, clr
  Register #(.width(32)) register_19 (.D(demultiplexer_1_out10), .Q(register_19_q), .clk(Clock));  // open: en, clr
  Register #(.width(32)) register_20 (.D(demultiplexer_1_out14), .Q(register_20_q), .clk(Clock));  // open: en, clr
  Register #(.width(32)) register_21 (.D(demultiplexer_1_out18), .Q(register_21_q), .clk(Clock));  // open: en, clr
  Register #(.width(32)) register_22 (.D(demultiplexer_1_out22), .Q(register_22_q), .clk(Clock));  // open: en, clr
  Register #(.width(32)) register_23 (.D(demultiplexer_1_out26), .Q(register_23_q), .clk(Clock));  // open: en, clr
  Register #(.width(32)) register_24 (.D(demultiplexer_1_out30), .Q(register_24_q), .clk(Clock));  // open: en, clr
  Register #(.width(32)) register_25 (.D(demultiplexer_1_out3), .Q(register_25_q), .clk(Clock));  // open: en, clr
  Register #(.width(32)) register_26 (.D(demultiplexer_1_out7), .Q(register_26_q), .clk(Clock));  // open: en, clr
  Register #(.width(32)) register_27 (.D(demultiplexer_1_out11), .Q(register_27_q), .clk(Clock));  // open: en, clr
  Register #(.width(32)) register_28 (.D(demultiplexer_1_out15), .Q(register_28_q), .clk(Clock));  // open: en, clr
  Register #(.width(32)) register_29 (.D(demultiplexer_1_out19), .Q(register_29_q), .clk(Clock));  // open: en, clr
  Register #(.width(32)) register_30 (.D(demultiplexer_1_out23), .Q(register_30_q), .clk(Clock));  // open: en, clr
  Register #(.width(32)) register_31 (.D(demultiplexer_1_out27), .Q(register_31_q), .clk(Clock));  // open: en, clr
  Register #(.width(32)) register_32 (.D(demultiplexer_1_out31), .Q(register_32_q), .clk(Clock));  // open: en, clr
  Multiplexer #(.select(5), .width(32), .enable("false")) multiplexer_1 (
    .in0(register_1_q), .in1(register_9_q), .in2(register_17_q), .in3(register_25_q), .in4(register_2_q),
    .in5(register_10_q), .in6(register_18_q), .in7(register_26_q), .in8(register_3_q), .in9(register_11_q),
    .in10(register_19_q), .in11(register_27_q), .in12(register_4_q), .in13(register_12_q),
    .in14(register_20_q), .in15(register_28_q), .in16(register_5_q), .in17(register_13_q),
    .in18(register_21_q), .in19(register_29_q), .in20(register_6_q), .in21(register_14_q),
    .in22(register_22_q), .in23(register_30_q), .in24(register_7_q), .in25(register_15_q),
    .in26(register_23_q), .in27(register_31_q), .in28(register_8_q), .in29(register_16_q),
    .in30(register_24_q), .in31(register_32_q), .out(Read_Data_1), .sel(Read_Reg_1));
  Multiplexer #(.select(5), .width(32), .enable("false")) multiplexer_2 (
    .in0(register_1_q), .in1(register_9_q), .in2(register_17_q), .in3(register_25_q), .in4(register_2_q),
    .in5(register_10_q), .in6(register_18_q), .in7(register_26_q), .in8(register_3_q), .in9(register_11_q),
    .in10(register_19_q), .in11(register_27_q), .in12(register_4_q), .in13(register_12_q),
    .in14(register_20_q), .in15(register_28_q), .in16(register_5_q), .in17(register_13_q),
    .in18(register_21_q), .in19(register_29_q), .in20(register_6_q), .in21(register_14_q),
    .in22(register_22_q), .in23(register_30_q), .in24(register_7_q), .in25(register_15_q),
    .in26(register_23_q), .in27(register_31_q), .in28(register_8_q), .in29(register_16_q),
    .in30(register_24_q), .in31(register_32_q), .out(Read_Data_2), .sel(Read_Reg_2));
endmodule

module Instruction_Memory (
  input  [31:0] Address,
  output [31:0] Instruction
);

  ROM #(.addrWidth(24), .dataWidth(32)) rom_1 (.addr(Address[23:0]), .data(Instruction));  // open: sel

  // Notes on the sheet:
  //   contents of rom_1 (hex, n*v repeats v):
  //   8c100000 8c110001 8c120002 8c130003 2128020 2709822 2329820 ac130004
endmodule
